// Logisim project Grimaldi_PO.circ as structural Verilog: 20 circuits, main circuit div_PO
module div_PO (
  input  [15:0] A,
  input  [15:0] B,
  input  s_a,
  input  s_q,
  input  l_a,
  input  l_b,
  input  l_q,
  input  clock,
  output comp1,
  output comp0,
  output [15:0] A_2,
  output [15:0] Q
);

  wire comparator_1_eq, comparator_1_gt;
  wire [15:0] adder_1_out, B_q, multiplexer_1_out, multiplexer_2_out, subtractor_1_out;

  Subtractor #(.width(16)) subtractor_1 (.a(A_2), .b(B_q), .out(subtractor_1_out));  // open: bin, bout
  Adder #(.width(16)) adder_1 (.a(Q), .b(16'h1), .out(adder_1_out));  // open: cin, cout
  Multiplexer #(.width(16)) multiplexer_1 (
    .in0(A), .in1(subtractor_1_out), .out(multiplexer_1_out), .sel(s_a));  // open: en
  Multiplexer #(.width(16)) multiplexer_2 (
    .in0({16{1'b0}}), .in1(adder_1_out), .out(multiplexer_2_out), .sel(s_q));  // open: en
  Register #(.width(16)) u_A (.D(multiplexer_1_out), .en(l_a), .Q(A_2), .clk(clock));  // open: clr
  Register #(.width(16)) u_B (.D(B), .en(l_b), .Q(B_q), .clk(clock));  // open: clr
  Register #(.width(16)) u_Q (.D(multiplexer_2_out), .en(l_q), .Q(Q), .clk(clock));  // open: clr
  Comparator #(.width(16)) comparator_1 (.a(A_2), .b(B_q), .gt(comparator_1_gt), .eq(comparator_1_eq));  // open: lt
  Comparator #(.width(16)) comparator_2 (.a(B_q), .b({16{1'b0}}), .gt(comp0));  // open: eq, lt
  or or_1 (comp1, comparator_1_gt, comparator_1_eq);

  // Notes on the sheet:
  //   fio5
  //   fio6
  //   fio0
  //   fio1
  //   fio2
  //   fio3
  //   fio4
endmodule

module div_PC (
  input  clk,
  input  reset,
  input  start,
  input  comp0,
  input  comp1,
  output l_q,
  output l_b,
  output l_a,
  output s_q,
  output s_a,
  output busy
);

  wire [1:0] multiplexer_1_out, multiplexer_2_out, multiplexer_3_out, multiplexer_4_out, multiplexer_5_out,
       res_q;

  Multiplexer #(.width(2)) multiplexer_1 (.in0(2'b00), .in1(2'b10), .out(multiplexer_1_out), .sel(comp1));  // open: en
  Multiplexer #(.width(2)) multiplexer_2 (.in0(2'b00), .in1(2'b01), .out(multiplexer_2_out), .sel(start));  // open: en
  Multiplexer #(.width(2)) multiplexer_3 (
    .in0(2'b00), .in1(multiplexer_1_out), .out(multiplexer_3_out), .sel(comp0));  // open: en
  Multiplexer #(.select(2), .width(2)) multiplexer_4 (
    .in0(multiplexer_2_out), .in1(multiplexer_3_out), .in2(2'b11), .in3(multiplexer_1_out),
    .out(multiplexer_4_out), .sel(res_q));  // open: en
  Multiplexer #(.width(2)) multiplexer_5 (
    .in0(multiplexer_4_out), .in1(2'b00), .out(multiplexer_5_out), .sel(reset));  // open: en
  Register #(.width(2)) res (.D(multiplexer_5_out), .Q(res_q), .clk(clk));  // open: en, clr
  Multiplexer #(.select(2), .width(5)) multiplexer_6 (
    .in0({2'b00, {2{start}}, 1'b0}), .in1(5'b00001), .in2(5'b10100), .in3(5'b01001),
    .out({s_a, s_q, l_a, l_b, l_q}), .sel(res_q));  // open: en
  Comparator #(.width(2), .mode("unsigned")) comparator_1 (.a(res_q), .b(2'b00), .eq(busy));  // open: gt, lt
endmodule

module div_PCPO (
  input  start,
  input  reset,
  input  clk,
  input  [15:0] ap,
  input  [15:0] bp,
  output [15:0] Ar,
  output [15:0] Qr,
  output busy
);

  wire div_pc_1_l_a, div_pc_1_l_b, div_pc_1_l_q, div_pc_1_s_a, div_pc_1_s_q, div_po_1_comp0, div_po_1_comp1;

  div_PC div_pc_1 (
    .clk(clk), .reset(reset), .start(start), .comp0(div_po_1_comp0), .comp1(div_po_1_comp1),
    .l_q(div_pc_1_l_q), .l_b(div_pc_1_l_b), .l_a(div_pc_1_l_a), .s_q(div_pc_1_s_q), .s_a(div_pc_1_s_a),
    .busy(busy));
  div_PO div_po_1 (
    .A(ap), .B(bp), .s_a(div_pc_1_s_a), .s_q(div_pc_1_s_q), .l_a(div_pc_1_l_a), .l_b(div_pc_1_l_b),
    .l_q(div_pc_1_l_q), .clock(clk), .comp1(div_po_1_comp1), .comp0(div_po_1_comp0), .A_2(Ar), .Q(Qr));
endmodule

module DIV (
  input  start,
  input  reset,
  input  [15:0] ap,
  input  [15:0] bp,
  output [15:0] Ar,
  output [15:0] Qr,
  output busy
);

  wire clk_out;

  Clock clk (.out(clk_out));
  div_PCPO div_pcpo_1 (.start(start), .reset(reset), .clk(clk_out), .ap(ap), .bp(bp), .Ar(Ar), .Qr(Qr), .busy(busy));
endmodule

module mult_PO (
  input  clock,
  input  [15:0] A,
  input  [15:0] B,
  input  [1:0] s_a,
  input  s_b,
  input  [1:0] s_t,
  input  l_a,
  input  l_b,
  input  l_t,
  output comp0,
  output comp1,
  output [31:0] T
);

  wire [15:0] A_q, B_q, bit_extender_2_out, multiplexer_1_out, multiplexer_2_out, subtractor_1_out;
  wire [31:0] adder_1_out, bit_extender_1_out, bit_extender_3_out, multiplexer_3_out;

  assign bit_extender_1_out = {{16{1'b0}}, B_q};  // Bit_Extender bit_extender_1
  Bit_Extender #(.in_width(32)) bit_extender_2 (.in(T), .out(bit_extender_2_out));
  assign bit_extender_3_out = {{16{1'b0}}, B};  // Bit_Extender bit_extender_3
  Subtractor #(.width(16)) subtractor_1 (.a(A_q), .b(16'h1), .out(subtractor_1_out));  // open: bin, bout
  Adder #(.width(32)) adder_1 (.a(T), .b(bit_extender_1_out), .out(adder_1_out));  // open: cin, cout
  Multiplexer #(.select(2), .width(16)) multiplexer_1 (
    .in0(A), .in1(bit_extender_2_out), .in2(subtractor_1_out), .out(multiplexer_1_out), .sel(s_a));  // open: in3, en
  Multiplexer #(.width(16)) multiplexer_2 (.in0(B), .in1(A), .out(multiplexer_2_out), .sel(s_b));  // open: en
  Multiplexer #(.select(2), .width(32)) multiplexer_3 (
    .in0(bit_extender_3_out), .in1({32{1'b0}}), .in2(adder_1_out), .out(multiplexer_3_out), .sel(s_t));  // open: in3, en
  Register #(.width(16)) u_A (.D(multiplexer_1_out), .en(l_a), .Q(A_q), .clk(clock));  // open: clr
  Register #(.width(16)) u_B (.D(multiplexer_2_out), .en(l_b), .Q(B_q), .clk(clock));  // open: clr
  Register #(.width(32)) u_T (.D(multiplexer_3_out), .en(l_t), .Q(T), .clk(clock));  // open: clr
  Comparator #(.width(16)) comparator_1 (.a(A_q), .b(B_q), .gt(comp0));  // open: eq, lt
  Comparator #(.width(16)) comparator_2 (.a(A_q), .b({16{1'b0}}), .gt(comp1));  // open: eq, lt

  // Notes on the sheet:
  //   fio4
  //   fio3
  //   fio0
  //   fio1
  //   fio2
  //   fio5
  //   fio6
  //   fio7
endmodule

module mult_PC (
  input  start,
  input  reset,
  input  comp0,
  input  comp1,
  input  clk,
  output [1:0] SA,
  output s_b,
  output [1:0] s_t,
  output l_a,
  output l_b,
  output l_t,
  output done
);

  wire [2:0] multiplexer_1_out, multiplexer_2_out, multiplexer_3_out, multiplexer_4_out, multiplexer_5_out,
       res_q;

  Multiplexer #(.width(3)) multiplexer_1 (
    .in0(3'b000), .in1(3'b110), .out(multiplexer_1_out), .sel(comp1));  // open: en
  Multiplexer #(.width(3)) multiplexer_2 (
    .in0(3'b000), .in1(3'b001), .out(multiplexer_2_out), .sel(start));  // open: en
  Multiplexer #(.width(3)) multiplexer_3 (
    .in0(3'b101), .in1(3'b010), .out(multiplexer_3_out), .sel(comp0));  // open: en
  Multiplexer #(.select(3), .width(3)) multiplexer_4 (
    .in0(multiplexer_2_out), .in1(multiplexer_3_out), .in2(3'b011), .in3(3'b100), .in4(3'b101),
    .in5(multiplexer_1_out), .in6(3'b111), .in7(multiplexer_1_out), .out(multiplexer_4_out), .sel(res_q));  // open: en
  Register #(.width(3)) res (.D(multiplexer_5_out), .Q(res_q), .clk(clk));  // open: en, clr
  Multiplexer #(.width(3)) multiplexer_5 (
    .in0(multiplexer_4_out), .in1(3'b000), .out(multiplexer_5_out), .sel(reset));  // open: en
  Multiplexer #(.select(3), .width(8)) multiplexer_6 (
    .in0({{5{1'b0}}, {2{start}}, 1'b0}), .in1({8{1'b0}}), .in2(8'h1), .in3(8'h22), .in4(8'h44), .in5(8'h9),
    .in6(8'h84), .in7(8'h11), .out({SA, s_b, s_t, l_a, l_b, l_t}), .sel(res_q));  // open: en
  Comparator #(.width(3), .mode("unsigned")) comparator_1 (.a(res_q), .b(3'b000), .eq(done));  // open: gt, lt
endmodule

module mult_PCPO (
  input  start,
  input  reset,
  input  clock,
  input  [15:0] A,
  input  [15:0] B,
  output [31:0] T,
  output done
);

  wire mult_pc_1_l_a, mult_pc_1_l_b, mult_pc_1_l_t, mult_pc_1_s_b, mult_po_1_comp0, mult_po_1_comp1;
  wire [1:0] mult_pc_1_s_t, mult_pc_1_sa;

  mult_PC mult_pc_1 (
    .start(start), .reset(reset), .comp0(mult_po_1_comp0), .comp1(mult_po_1_comp1), .clk(clock),
    .SA(mult_pc_1_sa), .s_b(mult_pc_1_s_b), .s_t(mult_pc_1_s_t), .l_a(mult_pc_1_l_a), .l_b(mult_pc_1_l_b),
    .l_t(mult_pc_1_l_t), .done(done));
  mult_PO mult_po_1 (
    .clock(clock), .A(A), .B(B), .s_a(mult_pc_1_sa), .s_b(mult_pc_1_s_b), .s_t(mult_pc_1_s_t),
    .l_a(mult_pc_1_l_a), .l_b(mult_pc_1_l_b), .l_t(mult_pc_1_l_t), .comp0(mult_po_1_comp0),
    .comp1(mult_po_1_comp1), .T(T));
endmodule

module MULT (
  input  [15:0] A,
  input  [15:0] B,
  input  start,
  input  reset,
  output [31:0] T,
  output Done
);

  wire clk_out;

  Clock clk (.out(clk_out));
  mult_PCPO mult_pcpo_1 (.start(start), .reset(reset), .clock(clk_out), .A(A), .B(B), .T(T), .done(Done));
endmodule

module mdc_PO (
  input  [15:0] A,
  input  [15:0] B,
  input  s_a,
  input  s_b,
  input  l_a,
  input  l_b,
  input  clock,
  output [15:0] A_2,
  output comp1,
  output comp0
);

  wire comparator_1_eq;
  wire [15:0] B_q, multiplexer_1_out, multiplexer_2_out, subtractor_1_out, subtractor_2_out;

  Subtractor #(.width(16)) subtractor_1 (.a(A_2), .b(B_q), .out(subtractor_1_out));  // open: bin, bout
  Subtractor #(.width(16)) subtractor_2 (.a(B_q), .b(A_2), .out(subtractor_2_out));  // open: bin, bout
  Multiplexer #(.width(16)) multiplexer_1 (
    .in0(A), .in1(subtractor_1_out), .out(multiplexer_1_out), .sel(s_a));  // open: en
  Multiplexer #(.width(16)) multiplexer_2 (
    .in0(B), .in1(subtractor_2_out), .out(multiplexer_2_out), .sel(s_b));  // open: en
  Register #(.width(16)) u_A (.D(multiplexer_1_out), .en(l_a), .Q(A_2), .clk(clock));  // open: clr
  Register #(.width(16)) u_B (.D(multiplexer_2_out), .en(l_b), .Q(B_q), .clk(clock));  // open: clr
  Comparator #(.width(16)) comparator_1 (.a(A_2), .b(B_q), .gt(comp1), .eq(comparator_1_eq));  // open: lt
  not not_1 (comp0, comparator_1_eq);

  // Notes on the sheet:
  //   fio4
  //   fio5
  //   fio0
  //   fio1
  //   fio2
  //   fio3
endmodule

module mdc_PC (
  input  start,
  input  reset,
  input  comp0,
  input  comp1,
  input  clk,
  output s_a,
  output s_b,
  output l_a,
  output l_b,
  output done
);

  wire [1:0] multiplexer_1_out, multiplexer_2_out, multiplexer_3_out, multiplexer_4_out, multiplexer_5_out,
       res_q;

  Multiplexer #(.width(2)) multiplexer_1 (.in0(2'b11), .in1(2'b10), .out(multiplexer_1_out), .sel(comp1));  // open: en
  Multiplexer #(.width(2)) multiplexer_2 (.in0(2'b00), .in1(2'b01), .out(multiplexer_2_out), .sel(start));  // open: en
  Multiplexer #(.width(2)) multiplexer_3 (
    .in0(2'b00), .in1(multiplexer_1_out), .out(multiplexer_3_out), .sel(comp0));  // open: en
  Multiplexer #(.select(2), .width(2)) multiplexer_4 (
    .in0(multiplexer_2_out), .in1(multiplexer_3_out), .in2(2'b01), .in3(2'b01), .out(multiplexer_4_out),
    .sel(res_q));  // open: en
  Multiplexer #(.width(2)) multiplexer_5 (
    .in0(multiplexer_4_out), .in1(2'b00), .out(multiplexer_5_out), .sel(reset));  // open: en
  Register #(.width(2)) res (.D(multiplexer_5_out), .Q(res_q), .clk(clk));  // open: en, clr
  Multiplexer #(.select(2), .width(4)) multiplexer_6 (
    .in0({2'b00, {2{start}}}), .in1(4'b0000), .in2(4'b1010), .in3(4'b0101), .out({s_a, s_b, l_a, l_b}),
    .sel(res_q));  // open: en
  Comparator #(.width(2), .mode("unsigned")) comparator_1 (.a(res_q), .b(2'b00), .eq(done));  // open: gt, lt
endmodule

module mdc_PCPO (
  input  [15:0] A,
  input  [15:0] B,
  input  start,
  input  reset,
  input  clk,
  output [15:0] Ar,
  output done
);

  wire mdc_pc_1_l_a, mdc_pc_1_l_b, mdc_pc_1_s_a, mdc_pc_1_s_b, mdc_po_1_comp0, mdc_po_1_comp1;

  mdc_PC mdc_pc_1 (
    .start(start), .reset(reset), .comp0(mdc_po_1_comp0), .comp1(mdc_po_1_comp1), .clk(clk),
    .s_a(mdc_pc_1_s_a), .s_b(mdc_pc_1_s_b), .l_a(mdc_pc_1_l_a), .l_b(mdc_pc_1_l_b), .done(done));
  mdc_PO mdc_po_1 (
    .A(A), .B(B), .s_a(mdc_pc_1_s_a), .s_b(mdc_pc_1_s_b), .l_a(mdc_pc_1_l_a), .l_b(mdc_pc_1_l_b),
    .clock(clk), .A_2(Ar), .comp1(mdc_po_1_comp1), .comp0(mdc_po_1_comp0));
endmodule

module MDC (
  input  [15:0] A,
  input  [15:0] B,
  input  start,
  input  reset,
  output [15:0] Ar,
  output Done
);

  wire clk_out;

  Clock clk (.out(clk_out));
  mdc_PCPO mdc_pcpo_1 (.A(A), .B(B), .start(start), .reset(reset), .clk(clk_out), .Ar(Ar), .done(Done));
endmodule

module pow_PO (
  input  [31:0] X,
  input  [31:0] Y,
  input  s_y,
  input  s_res,
  input  s_t,
  input  s_a,
  input  l_x,
  input  l_y,
  input  l_res,
  input  l_a,
  input  l_b,
  input  l_t,
  input  clock,
  output comp0,
  output comp1,
  output [31:0] res
);

  wire [31:0] a_q, adder_1_out, b_q, multiplexer_1_out, multiplexer_2_out, multiplexer_3_out,
       multiplexer_4_out, subtractor_1_out, subtractor_2_out, t_q, x_q, y_q;

  Subtractor #(.width(32)) subtractor_1 (.a(y_q), .b(32'h1), .out(subtractor_1_out));  // open: bin, bout
  Adder #(.width(32)) adder_1 (.a(t_q), .b(b_q), .out(adder_1_out));  // open: cin, cout
  Subtractor #(.width(32)) subtractor_2 (.a(a_q), .b(32'h1), .out(subtractor_2_out));  // open: bin, bout
  Multiplexer #(.width(32)) multiplexer_1 (
    .in0(Y), .in1(subtractor_1_out), .out(multiplexer_1_out), .sel(s_y));  // open: en
  Multiplexer #(.width(32)) multiplexer_2 (.in0(32'h1), .in1(t_q), .out(multiplexer_2_out), .sel(s_res));  // open: en
  Multiplexer #(.width(32)) multiplexer_3 (
    .in0({32{1'b0}}), .in1(adder_1_out), .out(multiplexer_3_out), .sel(s_t));  // open: en
  Multiplexer #(.width(32)) multiplexer_4 (
    .in0(x_q), .in1(subtractor_2_out), .out(multiplexer_4_out), .sel(s_a));  // open: en
  Register #(.width(32)) u_x (.D(X), .en(l_x), .Q(x_q), .clk(clock));  // open: clr
  Register #(.width(32)) u_y (.D(multiplexer_1_out), .en(l_y), .Q(y_q), .clk(clock));  // open: clr
  Register #(.width(32)) u_res (.D(multiplexer_2_out), .en(l_res), .Q(res), .clk(clock));  // open: clr
  Register #(.width(32)) t (.D(multiplexer_3_out), .en(l_t), .Q(t_q), .clk(clock));  // open: clr
  Register #(.width(32)) a (.D(multiplexer_4_out), .en(l_a), .Q(a_q), .clk(clock));  // open: clr
  Register #(.width(32)) b (.D(res), .en(l_b), .Q(b_q), .clk(clock));  // open: clr
  Comparator #(.width(32)) comparator_1 (.a(y_q), .b({32{1'b0}}), .gt(comp0));  // open: eq, lt
  Comparator #(.width(32)) comparator_2 (.a(a_q), .b({32{1'b0}}), .gt(comp1));  // open: eq, lt

  // Notes on the sheet:
  //   fio11
  //   fio12
  //   fio10
  //   fio0
  //   fio1
  //   fio2
  //   fio3
  //   fio4
  //   fio5
  //   fio6
  //   fio7
  //   fio8
  //   fio9
endmodule

module pow_PC (
  input  start,
  input  reset,
  input  comp0,
  input  comp1,
  input  clock,
  output s_y,
  output s_res,
  output s_t,
  output s_a,
  output l_x,
  output l_y,
  output l_res,
  output l_a,
  output l_b,
  output l_t,
  output Done
);

  wire [3:0] multiplexer_1_out, multiplexer_2_out, multiplexer_3_out, multiplexer_4_out, multiplexer_5_out,
       register_1_q;

  Multiplexer #(.width(4)) multiplexer_1 (
    .in0(4'b1001), .in1(4'b0111), .out(multiplexer_1_out), .sel(comp1));  // open: en
  Multiplexer #(.width(4)) multiplexer_2 (
    .in0(4'b0000), .in1(4'b0001), .out(multiplexer_2_out), .sel(start));  // open: en
  Multiplexer #(.width(4)) multiplexer_3 (
    .in0(4'b0000), .in1(4'b0011), .out(multiplexer_3_out), .sel(comp0));  // open: en
  Multiplexer #(.select(4), .width(4)) multiplexer_4 (
    .in0(multiplexer_2_out), .in1(4'b0010), .in2(multiplexer_3_out), .in3(4'b0100), .in4(4'b0101),
    .in5(4'b0110), .in6(multiplexer_1_out), .in7(4'b1000), .in8(multiplexer_1_out), .in9(4'b1010),
    .in10(4'b0010), .out(multiplexer_4_out), .sel(register_1_q));  // open: in11, in12, in13, in14, in15, en
  Multiplexer #(.width(4)) multiplexer_5 (
    .in0(multiplexer_4_out), .in1(4'b0001), .out(multiplexer_5_out), .sel(reset));  // open: en
  Register #(.width(4)) register_1 (.D(multiplexer_5_out), .Q(register_1_q), .clk(clock));  // open: en, clr
  Multiplexer #(.select(4), .width(10)) multiplexer_6 (
    .in0({4'b0000, {2{start}}, 4'b0000}), .in1(10'h8), .in2({10{1'b0}}), .in3(10'h4), .in4(10'h2),
    .in5(10'h1), .in6({10{1'b0}}), .in7(10'h44), .in8(10'h81), .in9(10'h108), .in10(10'h210),
    .out({s_y, s_res, s_t, s_a, l_x, l_y, l_res, l_a, l_b, l_t}), .sel(register_1_q));  // open: in11, in12, in13, in14, in15, en
  Comparator #(.width(4), .mode("unsigned")) comparator_1 (.a(register_1_q), .b(4'b0000), .eq(Done));  // open: gt, lt
endmodule

module pow_PCPO (
  input  [31:0] X,
  input  [31:0] Y,
  input  start,
  input  reset,
  input  clock,
  output [31:0] res,
  output done
);

  wire pow_pc_1_l_a, pow_pc_1_l_b, pow_pc_1_l_res, pow_pc_1_l_t, pow_pc_1_l_x, pow_pc_1_l_y, pow_pc_1_s_a,
       pow_pc_1_s_res, pow_pc_1_s_t, pow_pc_1_s_y, pow_po_1_comp0, pow_po_1_comp1;

  pow_PC pow_pc_1 (
    .start(start), .reset(reset), .comp0(pow_po_1_comp0), .comp1(pow_po_1_comp1), .clock(clock),
    .s_y(pow_pc_1_s_y), .s_res(pow_pc_1_s_res), .s_t(pow_pc_1_s_t), .s_a(pow_pc_1_s_a), .l_x(pow_pc_1_l_x),
    .l_y(pow_pc_1_l_y), .l_res(pow_pc_1_l_res), .l_a(pow_pc_1_l_a), .l_b(pow_pc_1_l_b), .l_t(pow_pc_1_l_t),
    .Done(done));
  pow_PO pow_po_1 (
    .X(X), .Y(Y), .s_y(pow_pc_1_s_y), .s_res(pow_pc_1_s_res), .s_t(pow_pc_1_s_t), .s_a(pow_pc_1_s_a),
    .l_x(pow_pc_1_l_x), .l_y(pow_pc_1_l_y), .l_res(pow_pc_1_l_res), .l_a(pow_pc_1_l_a), .l_b(pow_pc_1_l_b),
    .l_t(pow_pc_1_l_t), .clock(clock), .comp0(pow_po_1_comp0), .comp1(pow_po_1_comp1), .res(res));
endmodule

module POW (
  input  [31:0] X,
  input  [31:0] Y,
  input  start,
  input  reset,
  output [31:0] res,
  output Done
);

  wire clk_out;

  Clock clk (.out(clk_out));
  pow_PCPO pow_pcpo_1 (.X(X), .Y(Y), .start(start), .reset(reset), .clock(clk_out), .res(res), .done(Done));
endmodule

module fib_PO (
  input  [31:0] n,
  input  s_atual,
  input  s_anterior,
  input  s_i,
  input  l_atual,
  input  l_anterior,
  input  l_i,
  input  l_n,
  input  clock,
  output comp0,
  output [31:0] Atual,
  output comp1
);

  wire comparator_1_eq, comparator_1_gt;
  wire [31:0] adder_1_out, adder_2_out, Anterior_q, i_q, multiplexer_1_out, multiplexer_2_out,
       multiplexer_3_out, N_q, subtractor_1_out;

  Adder #(.width(32)) adder_1 (.a(Atual), .b(Anterior_q), .out(adder_1_out));  // open: cin, cout
  Subtractor #(.width(32)) subtractor_1 (.a(Atual), .b(Anterior_q), .out(subtractor_1_out));  // open: bin, bout
  Adder #(.width(32)) adder_2 (.a(i_q), .b(32'h1), .out(adder_2_out));  // open: cin, cout
  Multiplexer #(.width(32)) multiplexer_1 (
    .in0(32'h1), .in1(adder_1_out), .out(multiplexer_1_out), .sel(s_atual));  // open: en
  Multiplexer #(.width(32)) multiplexer_2 (
    .in0({32{1'b0}}), .in1(subtractor_1_out), .out(multiplexer_2_out), .sel(s_anterior));  // open: en
  Multiplexer #(.width(32)) multiplexer_3 (
    .in0(32'h1), .in1(adder_2_out), .out(multiplexer_3_out), .sel(s_i));  // open: en
  Register #(.width(32)) u_N (.D(n), .en(l_n), .Q(N_q), .clk(clock));  // open: clr
  Register #(.width(32)) u_Atual (.D(multiplexer_1_out), .en(l_atual), .Q(Atual), .clk(clock));  // open: clr
  Register #(.width(32)) Anterior (.D(multiplexer_2_out), .en(l_anterior), .Q(Anterior_q), .clk(clock));  // open: clr
  Register #(.width(32)) i (.D(multiplexer_3_out), .en(l_i), .Q(i_q), .clk(clock));  // open: clr
  Comparator #(.width(32)) comparator_1 (.a(N_q), .b(i_q), .gt(comparator_1_gt), .eq(comparator_1_eq));  // open: lt
  or or_1 (comp0, comparator_1_gt, comparator_1_eq);
  Comparator #(.width(32)) comparator_2 (.a(i_q), .b(32'h1), .eq(comp1));  // open: gt, lt

  // Notes on the sheet:
  //   fio6
  //   fio7
  //   fio8
  //   fio0
  //   fio1
  //   fio2
  //   fio4
  //   fio5
  //   fio3
endmodule

module fib_PC (
  input  reset,
  input  start,
  input  comp0,
  input  comp1,
  input  clock,
  output s_atual,
  output s_anterior,
  output s_i,
  output l_atual,
  output l_anterior,
  output l_i,
  output l_n,
  output Done
);

  wire [2:0] multiplexer_1_out, multiplexer_2_out, multiplexer_3_out, multiplexer_4_out, multiplexer_5_out,
       register_1_q;

  Multiplexer #(.width(3)) multiplexer_1 (
    .in0(3'b101), .in1(3'b011), .out(multiplexer_1_out), .sel(comp1));  // open: en
  Multiplexer #(.width(3)) multiplexer_2 (
    .in0(3'b000), .in1(3'b001), .out(multiplexer_2_out), .sel(start));  // open: en
  Multiplexer #(.width(3)) multiplexer_3 (
    .in0(3'b000), .in1(multiplexer_1_out), .out(multiplexer_3_out), .sel(comp0));  // open: en
  Multiplexer #(.select(3), .width(3)) multiplexer_4 (
    .in0(multiplexer_2_out), .in1(3'b010), .in2(multiplexer_3_out), .in3(3'b100), .in4(3'b111), .in5(3'b110),
    .in6(3'b111), .in7(multiplexer_3_out), .out(multiplexer_4_out), .sel(register_1_q));  // open: en
  Multiplexer #(.width(3)) multiplexer_5 (
    .in0(multiplexer_4_out), .in1(3'b000), .out(multiplexer_5_out), .sel(reset));  // open: en
  Register #(.width(3)) register_1 (.D(multiplexer_5_out), .Q(register_1_q), .clk(clock));  // open: en, clr
  Multiplexer #(.select(3), .width(7)) multiplexer_6 (
    .in0({{6{1'b0}}, start}), .in1(7'b0000010), .in2({7{1'b0}}), .in3(7'b0001000), .in4(7'b0000100),
    .in5(7'b1001000), .in6(7'b0100100), .in7(7'b0010010),
    .out({s_atual, s_anterior, s_i, l_atual, l_anterior, l_i, l_n}), .sel(register_1_q));  // open: en
  Comparator #(.width(3), .mode("unsigned")) comparator_1 (.a(register_1_q), .b(3'b000), .eq(Done));  // open: gt, lt
endmodule

module fib_PCPO (
  input  [31:0] n,
  input  start,
  input  reset,
  input  clock,
  output [31:0] Atual,
  output Done
);

  wire fib_pc_1_l_anterior, fib_pc_1_l_atual, fib_pc_1_l_i, fib_pc_1_l_n, fib_pc_1_s_anterior,
       fib_pc_1_s_atual, fib_pc_1_s_i, fib_po_1_comp0, fib_po_1_comp1;

  fib_PC fib_pc_1 (
    .reset(reset), .start(start), .comp0(fib_po_1_comp0), .comp1(fib_po_1_comp1), .clock(clock),
    .s_atual(fib_pc_1_s_atual), .s_anterior(fib_pc_1_s_anterior), .s_i(fib_pc_1_s_i),
    .l_atual(fib_pc_1_l_atual), .l_anterior(fib_pc_1_l_anterior), .l_i(fib_pc_1_l_i), .l_n(fib_pc_1_l_n),
    .Done(Done));
  fib_PO fib_po_1 (
    .n(n), .s_atual(fib_pc_1_s_atual), .s_anterior(fib_pc_1_s_anterior), .s_i(fib_pc_1_s_i),
    .l_atual(fib_pc_1_l_atual), .l_anterior(fib_pc_1_l_anterior), .l_i(fib_pc_1_l_i), .l_n(fib_pc_1_l_n),
    .clock(clock), .comp0(fib_po_1_comp0), .Atual(Atual), .comp1(fib_po_1_comp1));
endmodule

module FIB (
  input  [31:0] n,
  input  start,
  input  reset,
  output [31:0] Atual,
  output Done
);

  wire clk_out;

  Clock clk (.out(clk_out));
  fib_PCPO fib_pcpo_1 (.n(n), .start(start), .reset(reset), .clock(clk_out), .Atual(Atual), .Done(Done));
endmodule
